# Fritzing sketch schema (saved by Fritzing 1.0.4)

parts:
  Rotary_Encoder1 = IDUINO Rotary Encoder SE055
  Sensor1 = TTP223B Capacitive Touch Sensor Module
  Power_supply_5v_3-10A = HLK-PM01
  Part1 = Adafruit MAX9814 Electret Microphone Amplifier [part_number="Adafruit #1713"]
  Squix1 = OLED 0.96" 128x64 I2C SSD1306
  D1_1N4001-1N4007 = Diode [package=diode-1n4001]
  R1 = Resistor [tolerance=±5% power=0.25W resistance=470 package=THT]
  U1 = ESP32-38PinWide [part_number=ESP32-38PinWide]
  U2 = WS2812 RGB LED strip
  C2_470mF = Capacitor Polarized [package=cpol-radial-100uf-25v]
  C1_10mF = Capacitor Polarized [package=cpol-radial-100uf-25v]
  R2 = Resistor [tolerance=±5% power=0.25W resistance=470 package=THT]
  R3 = Resistor [tolerance=±5% power=0.25W resistance=470 package=THT]
  R1-R4 = Resistor [tolerance=±5% power=0.25W resistance=470 package=THT]
  U3 = WS2812 RGB LED strip
  U4 = WS2812 RGB LED strip
  U5 = WS2812 RGB LED strip
  LDR = Photocell (LDR) [power=0.25W dark_resistance_@0.01lx=300kΩ light_resistance_@100lx=400Ω luminance=10lx package=THT]
  R6 = Resistor [tolerance=±5% power=0.25W resistance=10k package=THT]

nets:
  GND: Rotary_Encoder1.GND, Sensor1.GND, Power_supply_5v_3-10A.-Vo, Part1.GND, Squix1.GND, U1.GPIO11, U2.GND, C2_470mF.-, C1_10mF.-, U3.GND, U4.GND, U5.GND
  VDD: Rotary_Encoder1.VDD, Sensor1.VCC, Part1.VDD, Squix1.VCC, U1.GPIO10
  N1: Rotary_Encoder1.SW, U1.GPIO5
  N2: Rotary_Encoder1.DT, U1.GPIO18
  N3: Rotary_Encoder1.CLK, U1.GPIO19
  N4: Sensor1.SIG, U1.GPIO32
  VCC: Power_supply_5v_3-10A.+Vo, D1_1N4001-1N4007.A, C2_470mF.+, U3.VCC, U4.VCC, U5.VCC
  N5: Part1.OUTPUT, U1.GPIO35
  N6: Squix1.SCL, U1.GPIO22
  N7: Squix1.SCA, U1.GPIO21
  N8: D1_1N4001-1N4007.C, U1.VIN
  N9: R1.Pin_0, U1.GPIO33
  N10: R1.Pin_1, U2.DIN
  N11: U1.3.3, LDR.pin_1
  N12: U1.EN, C1_10mF.+
  N13: U1.GPIO34, LDR.pin_0, R6.Pin_1
  N14: U1.GPIO25, R2.Pin_0
  N15: U1.GPIO26, R3.Pin_0
  N16: U1.GPIO27, R1-R4.Pin_0
  N17: U1.GND, R6.Pin_0
  N18: R2.Pin_1, U3.DIN
  N19: R3.Pin_1, U4.DIN
  N20: R1-R4.Pin_1, U5.DIN

custom parts:
  IDUINO Rotary Encoder SE055: https://www.conrad.com/p/iduino-rotary-encoder-1-pcs-se055-1485328
  TTP223B Capacitive Touch Sensor Module: The TTP223B capacitive touch sensor module uses the TTP223B IC. The appropriate voltage is approximately 2 to 5.5 volts.
  Adafruit MAX9814 Electret Microphone Amplifier: Add an ear to your project with this well-designed electret microphone amplifier with AGC. This fully assembled and tested board comes with a 20-20KHz electret microphone soldered on. For the amplification, we use the Maxim MAX9814, a specialty chip that is designed for amplifying electret microphones in situations where the loudness of the audio isn't predictable. This fancy microphone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
  ESP32-38PinWide: Generic 38-Pin ESP32 with wide format (only access to one side of pins on a breadboard) based on Stephen Lilley's HiLetgo ESP-WROOM-32 ESP32 ESP-32S Development Board.
  WS2812 RGB LED strip: WS2812 strip
